# Fritzing sketch CellularTemperatureSensorNode (saved by Fritzing 0.9.3b)

parts:
  U1 = ESP32-38PinWide [part_number=ESP32-38PinWide]
  GSM_SIM_GPSR_SMS_SIM900_SIM1 = SIM800L [package=THT]
  DS1 = DS18B20 1-Wire Temperature Sensor [part_number=DS18B20]
  D1 = Rectifier Diode [part_number=1N4001 package="Melf DO-213 AB [SMD]"]
  R1 = Resistor [tolerance=±5% resistance=4.7k package="0805 [SMD]"]

nets:
  N1: U1.3.3, DS1.VDD, R1.Pin_0
  N2: U1.GPIO11, GSM_SIM_GPSR_SMS_SIM900_SIM1.GND
  N3: U1.VIN, D1.anode
  N4: U1.GPIO4, DS1.DQ, R1.Pin_1
  N5: U1.GPIO16, GSM_SIM_GPSR_SMS_SIM900_SIM1.SIM_TXD
  N6: U1.GPIO17, GSM_SIM_GPSR_SMS_SIM900_SIM1.SIM_RXD
  GND: U1.GND, DS1.GND
  N7: GSM_SIM_GPSR_SMS_SIM900_SIM1.5V, D1.cathode

custom parts:
  ESP32-38PinWide: Generic 38-Pin ESP32 with wide format (only access to one side of pins on a breadboard) based on Stephen Lilley's HiLetgo ESP-WROOM-32 ESP32 ESP-32S Development Board.
